// Logisim project MIPSpipeline.circ as structural Verilog: 13 circuits, main circuit main
module main (
);

  wire adder_1_cout, adder_2_cout, alu_1_zero, and_1_out, CLK, ex_mem_1_out_12, ex_mem_1_out_13,
       ex_mem_1_out_14, ex_mem_1_out_15, ex_mem_1_out_16, ex_mem_1_out_17, hazardunit_1_flush,
       hazardunit_1_out_4, hazardunit_1_out_6, id_ex_1_out_18, id_ex_1_out_19, id_ex_1_out_20,
       id_ex_1_out_21, id_ex_1_out_22, id_ex_1_out_23, id_ex_1_out_24, mem_wb_1_out_7, mem_wb_1_out_8;
  wire [1:0] forwardingunit_1_out_7, forwardingunit_1_out_8;
  wire [3:0] controlunit_1_out_10, id_ex_1_out_25;
  wire [4:0] ex_mem_1_out_21, id_ex_1_out_26, id_ex_1_out_32, id_ex_1_out_33, intructionformater_1_out_3,
       intructionformater_1_out_4, intructionformater_1_out_6, intructionformater_1_out_7, mem_wb_1_out_11,
       multiplexer_3_out;
  wire [5:0] intructionformater_1_out_2, intructionformater_1_out_8;
  wire [6:0] controlunit_1_out_3;
  wire [15:0] adder_1_out, adder_2_out, ex_mem_1_out_19, id_ex_1_out_29, id_ex_1_out_30, if_id_1_out_6,
       intructionformater_1_out_5, multiplexer_1_out, multiplexer_2_out, register_1_q, shifter_1_out;
  wire [31:0] alu_1_out_6, bit_extender_1_out, dm_1_out_6, ex_mem_1_out_18, ex_mem_1_out_20, id_ex_1_out_27,
       id_ex_1_out_28, if_id_1_out_5, im_1_out_2, mem_wb_1_out_9, mem_wb_1_out_10, multiplexer_4_out,
       multiplexer_5_out, multiplexer_6_out, multiplexer_7_out, registers_1_out_7, registers_1_out_8;

  Clock clock_1 (.out(CLK));
  Register #(.width(16)) register_1 (
    .D(multiplexer_1_out), .en(hazardunit_1_out_6), .clk(CLK), .Q(register_1_q));  // open: clr
  Multiplexer #(.width(16)) multiplexer_1 (
    .in0(adder_1_out), .in1(ex_mem_1_out_19), .out(multiplexer_1_out), .sel(and_1_out));
  Adder #(.width(16)) adder_1 (.a(register_1_q), .b(16'h4), .out(adder_1_out), .cin(1'b0), .cout(adder_1_cout));
  IM im_1 (.in_1(register_1_q), .out_2(im_1_out_2));
  IF_ID if_id_1 (
    .in_2(im_1_out_2), .in_3(adder_1_out), .in_1(hazardunit_1_out_4), .in_4(CLK), .out_5(if_id_1_out_5),
    .out_6(if_id_1_out_6));
  IntructionFormater intructionformater_1 (
    .in_1(if_id_1_out_5), .out_6(intructionformater_1_out_6), .out_7(intructionformater_1_out_7),
    .out_8(intructionformater_1_out_8), .out_2(intructionformater_1_out_2),
    .out_3(intructionformater_1_out_3), .out_4(intructionformater_1_out_4), .out_5(intructionformater_1_out_5));
  ControlUnit controlunit_1 (
    .in_1(intructionformater_1_out_8), .in_2(intructionformater_1_out_2), .out_4(controlunit_1_out_3[1]),
    .out_3(controlunit_1_out_3[0]), .out_5(controlunit_1_out_3[2]), .out_8(controlunit_1_out_3[5]),
    .out_9(controlunit_1_out_3[6]), .out_10(controlunit_1_out_10), .out_6(controlunit_1_out_3[3]),
    .out_7(controlunit_1_out_3[4]));
  Multiplexer #(.width(16)) multiplexer_2 (
    .in0({intructionformater_1_out_3, controlunit_1_out_10, controlunit_1_out_3}), .in1({16{1'b0}}),
    .out(multiplexer_2_out), .sel(hazardunit_1_flush));
  registers registers_1 (
    .in_1(intructionformater_1_out_7), .in_4(intructionformater_1_out_6), .in_5(mem_wb_1_out_8),
    .in_6(mem_wb_1_out_11), .CLK(CLK), .in_3(multiplexer_7_out), .out_7(registers_1_out_7),
    .out_8(registers_1_out_8));
  HazardUnit hazardunit_1 (
    .MemRead(if_id_1_out_5), .in_1(id_ex_1_out_32), .in_3(id_ex_1_out_18), .out_4(hazardunit_1_out_4),
    .Flush(hazardunit_1_flush), .out_6(hazardunit_1_out_6));
  ID_EX id_ex_1 (
    .in_1(multiplexer_2_out[0]), .in_2(multiplexer_2_out[1]), .in_3(multiplexer_2_out[2]),
    .in_4(multiplexer_2_out[3]), .RegDst(multiplexer_2_out[4]), .Branch(multiplexer_2_out[5]),
    .ALUsrc(multiplexer_2_out[6]), .in_8(multiplexer_2_out[10:7]), .in_9(multiplexer_2_out[15:11]),
    .in_14(intructionformater_1_out_7), .in_15(intructionformater_1_out_6),
    .in_16(intructionformater_1_out_4), .in_10(registers_1_out_7), .in_11(registers_1_out_8),
    .in_12(intructionformater_1_out_5), .in_13(if_id_1_out_6), .out_32(id_ex_1_out_32),
    .out_33(id_ex_1_out_33), .out_27(id_ex_1_out_27), .out_28(id_ex_1_out_28), .out_29(id_ex_1_out_29),
    .out_30(id_ex_1_out_30), .out_18(id_ex_1_out_18), .out_19(id_ex_1_out_19), .out_20(id_ex_1_out_20),
    .out_21(id_ex_1_out_21), .out_22(id_ex_1_out_22), .out_23(id_ex_1_out_23), .out_24(id_ex_1_out_24),
    .out_25(id_ex_1_out_25), .out_26(id_ex_1_out_26));  // open: CLK, out_31
  Multiplexer #(.width(5)) multiplexer_3 (
    .in0(id_ex_1_out_32), .in1(id_ex_1_out_33), .out(multiplexer_3_out), .sel(id_ex_1_out_22));
  assign bit_extender_1_out = {{16{id_ex_1_out_29[15]}}, id_ex_1_out_29};  // Bit_Extender bit_extender_1
  Shifter #(.width(16)) shifter_1 (.in(id_ex_1_out_29), .\dist (4'b0010), .out(shifter_1_out));
  Adder #(.width(16)) adder_2 (
    .a(id_ex_1_out_30), .b(shifter_1_out), .out(adder_2_out), .cin(1'b0), .cout(adder_2_cout));
  Multiplexer #(.select(2), .width(32)) multiplexer_4 (
    .in0(id_ex_1_out_27), .in1(ex_mem_1_out_18), .in2(mem_wb_1_out_10), .in3({32{1'b0}}),
    .out(multiplexer_4_out), .sel(forwardingunit_1_out_7));
  Multiplexer #(.select(2), .width(32)) multiplexer_5 (
    .in0(id_ex_1_out_28), .in1(ex_mem_1_out_18), .in2(mem_wb_1_out_10), .in3({32{1'b0}}),
    .out(multiplexer_5_out), .sel(forwardingunit_1_out_8));
  ForwardingUnit forwardingunit_1 (
    .in_5(id_ex_1_out_21), .in_2(id_ex_1_out_32), .in_6(ex_mem_1_out_21), .in_3(id_ex_1_out_33),
    .in_4(multiplexer_3_out), .in_1(ex_mem_1_out_15), .out_8(forwardingunit_1_out_8),
    .out_7(forwardingunit_1_out_7));
  Multiplexer #(.width(32)) multiplexer_6 (
    .in0(multiplexer_5_out), .in1(bit_extender_1_out), .out(multiplexer_6_out), .sel(id_ex_1_out_24));
  ALU alu_1 (
    .in_3(id_ex_1_out_26), .in_1(multiplexer_4_out), .in_2(multiplexer_6_out), .in_4(id_ex_1_out_25),
    .ZERO(alu_1_zero), .out_6(alu_1_out_6));
  and and_1 (and_1_out, ex_mem_1_out_17, ex_mem_1_out_16);
  EX_MEM ex_mem_1 (
    .in_9(multiplexer_5_out), .in_10(multiplexer_3_out), .CLK(CLK), .in_8(adder_2_out),
    .in_1(id_ex_1_out_18), .in_2(id_ex_1_out_19), .in_3(id_ex_1_out_20), .in_4(id_ex_1_out_21),
    .Branch(id_ex_1_out_23), .Zero(alu_1_zero), .in_7(alu_1_out_6), .out_20(ex_mem_1_out_20),
    .out_21(ex_mem_1_out_21), .out_12(ex_mem_1_out_12), .out_13(ex_mem_1_out_13), .out_14(ex_mem_1_out_14),
    .out_15(ex_mem_1_out_15), .out_16(ex_mem_1_out_16), .out_17(ex_mem_1_out_17), .out_18(ex_mem_1_out_18),
    .out_19(ex_mem_1_out_19));
  DM dm_1 (
    .in_3(ex_mem_1_out_12), .in_1(ex_mem_1_out_18), .CLK(CLK), .in_5(ex_mem_1_out_20),
    .in_2(ex_mem_1_out_13), .out_6(dm_1_out_6));
  MEM_WB mem_wb_1 (
    .in_5(ex_mem_1_out_21), .in_1(ex_mem_1_out_14), .in_2(ex_mem_1_out_15), .in_3(dm_1_out_6),
    .in_4(ex_mem_1_out_18), .CLK(CLK), .out_7(mem_wb_1_out_7), .out_8(mem_wb_1_out_8),
    .out_9(mem_wb_1_out_9), .out_10(mem_wb_1_out_10), .out_11(mem_wb_1_out_11));
  Multiplexer #(.width(32)) multiplexer_7 (
    .in0(mem_wb_1_out_10), .in1(mem_wb_1_out_9), .out(multiplexer_7_out), .sel(mem_wb_1_out_7));
  // also tied to GND on the sheet: {adder_1_cout, adder_2_cout}

  // Notes on the sheet:
  //   PC
endmodule

module registers (
  input  [4:0] in_1,
  input  CLK,
  input  [31:0] in_3,
  input  [4:0] in_4,
  input  in_5,
  input  [4:0] in_6,
  output [31:0] out_7,
  output [31:0] out_8
);

  wire demultiplexer_1_out1, demultiplexer_1_out2, demultiplexer_1_out3, demultiplexer_1_out4,
       demultiplexer_1_out5, demultiplexer_1_out6, demultiplexer_1_out7, demultiplexer_1_out8,
       demultiplexer_1_out9, demultiplexer_1_out10, demultiplexer_1_out11, demultiplexer_1_out12,
       demultiplexer_1_out13, demultiplexer_1_out14, demultiplexer_1_out15, demultiplexer_1_out16,
       demultiplexer_1_out17, demultiplexer_1_out18, demultiplexer_1_out19, demultiplexer_1_out20,
       demultiplexer_1_out21, demultiplexer_1_out22, demultiplexer_1_out23, demultiplexer_1_out24,
       demultiplexer_1_out25, demultiplexer_1_out26, demultiplexer_1_out27, demultiplexer_1_out28,
       demultiplexer_1_out29, demultiplexer_1_out30, demultiplexer_1_out31;
  wire [31:0] register_1_q, register_2_q, register_3_q, register_4_q, register_5_q, register_6_q,
       register_7_q, register_8_q, register_9_q, register_10_q, register_11_q, register_12_q, register_13_q,
       register_14_q, register_15_q, register_16_q, register_17_q, register_18_q, register_19_q,
       register_20_q, register_21_q, register_22_q, register_23_q, register_24_q, register_25_q,
       register_26_q, register_27_q, register_28_q, register_29_q, register_30_q, register_31_q,
       register_32_q;

  Demultiplexer #(.select(5)) demultiplexer_1 (
    .out1(demultiplexer_1_out1), .out2(demultiplexer_1_out2), .out3(demultiplexer_1_out3),
    .out4(demultiplexer_1_out4), .out5(demultiplexer_1_out5), .out6(demultiplexer_1_out6),
    .out7(demultiplexer_1_out7), .out8(demultiplexer_1_out8), .out9(demultiplexer_1_out9),
    .out10(demultiplexer_1_out10), .out11(demultiplexer_1_out11), .out12(demultiplexer_1_out12),
    .out13(demultiplexer_1_out13), .out14(demultiplexer_1_out14), .out15(demultiplexer_1_out15),
    .out16(demultiplexer_1_out16), .out17(demultiplexer_1_out17), .out18(demultiplexer_1_out18),
    .out19(demultiplexer_1_out19), .out20(demultiplexer_1_out20), .out21(demultiplexer_1_out21),
    .out22(demultiplexer_1_out22), .out23(demultiplexer_1_out23), .out24(demultiplexer_1_out24),
    .out25(demultiplexer_1_out25), .out26(demultiplexer_1_out26), .out27(demultiplexer_1_out27),
    .out28(demultiplexer_1_out28), .out29(demultiplexer_1_out29), .out30(demultiplexer_1_out30),
    .out31(demultiplexer_1_out31), .in(in_5), .sel(in_6));  // open: out0
  Register #(.width(32)) register_1 (.D(in_3), .en(1'b0), .clk(CLK), .Q(register_1_q));  // open: clr
  Register #(.width(32)) register_2 (.D(in_3), .en(demultiplexer_1_out1), .clk(CLK), .Q(register_2_q));  // open: clr
  Register #(.width(32)) register_3 (.D(in_3), .en(demultiplexer_1_out2), .clk(CLK), .Q(register_3_q));  // open: clr
  Register #(.width(32)) register_4 (.D(in_3), .en(demultiplexer_1_out3), .clk(CLK), .Q(register_4_q));  // open: clr
  Register #(.width(32)) register_5 (.D(in_3), .en(demultiplexer_1_out4), .clk(CLK), .Q(register_5_q));  // open: clr
  Register #(.width(32)) register_6 (.D(in_3), .en(demultiplexer_1_out5), .clk(CLK), .Q(register_6_q));  // open: clr
  Register #(.width(32)) register_7 (.D(in_3), .en(demultiplexer_1_out6), .clk(CLK), .Q(register_7_q));  // open: clr
  Register #(.width(32)) register_8 (.D(in_3), .en(demultiplexer_1_out7), .clk(CLK), .Q(register_8_q));  // open: clr
  Register #(.width(32)) register_9 (.D(in_3), .en(demultiplexer_1_out8), .clk(CLK), .Q(register_9_q));  // open: clr
  Register #(.width(32)) register_10 (.D(in_3), .en(demultiplexer_1_out9), .clk(CLK), .Q(register_10_q));  // open: clr
  Register #(.width(32)) register_11 (.D(in_3), .en(demultiplexer_1_out10), .clk(CLK), .Q(register_11_q));  // open: clr
  Register #(.width(32)) register_12 (.D(in_3), .en(demultiplexer_1_out11), .clk(CLK), .Q(register_12_q));  // open: clr
  Register #(.width(32)) register_13 (.D(in_3), .en(demultiplexer_1_out12), .clk(CLK), .Q(register_13_q));  // open: clr
  Register #(.width(32)) register_14 (.D(in_3), .en(demultiplexer_1_out13), .clk(CLK), .Q(register_14_q));  // open: clr
  Register #(.width(32)) register_15 (.D(in_3), .en(demultiplexer_1_out14), .clk(CLK), .Q(register_15_q));  // open: clr
  Register #(.width(32)) register_16 (.D(in_3), .en(demultiplexer_1_out15), .clk(CLK), .Q(register_16_q));  // open: clr
  Register #(.width(32)) register_17 (.D(in_3), .en(demultiplexer_1_out16), .clk(CLK), .Q(register_17_q));  // open: clr
  Register #(.width(32)) register_18 (.D(in_3), .en(demultiplexer_1_out17), .clk(CLK), .Q(register_18_q));  // open: clr
  Register #(.width(32)) register_19 (.D(in_3), .en(demultiplexer_1_out18), .clk(CLK), .Q(register_19_q));  // open: clr
  Register #(.width(32)) register_20 (.D(in_3), .en(demultiplexer_1_out19), .clk(CLK), .Q(register_20_q));  // open: clr
  Register #(.width(32)) register_21 (.D(in_3), .en(demultiplexer_1_out20), .clk(CLK), .Q(register_21_q));  // open: clr
  Register #(.width(32)) register_22 (.D(in_3), .en(demultiplexer_1_out21), .clk(CLK), .Q(register_22_q));  // open: clr
  Register #(.width(32)) register_23 (.D(in_3), .en(demultiplexer_1_out22), .clk(CLK), .Q(register_23_q));  // open: clr
  Register #(.width(32)) register_24 (.D(in_3), .en(demultiplexer_1_out23), .clk(CLK), .Q(register_24_q));  // open: clr
  Register #(.width(32)) register_25 (.D(in_3), .en(demultiplexer_1_out24), .clk(CLK), .Q(register_25_q));  // open: clr
  Register #(.width(32)) register_26 (.D(in_3), .en(demultiplexer_1_out25), .clk(CLK), .Q(register_26_q));  // open: clr
  Register #(.width(32)) register_27 (.D(in_3), .en(demultiplexer_1_out26), .clk(CLK), .Q(register_27_q));  // open: clr
  Register #(.width(32)) register_28 (.D(in_3), .en(demultiplexer_1_out27), .clk(CLK), .Q(register_28_q));  // open: clr
  Register #(.width(32)) register_29 (.D(in_3), .en(demultiplexer_1_out28), .clk(CLK), .Q(register_29_q));  // open: clr
  Register #(.width(32)) register_30 (.D(in_3), .en(demultiplexer_1_out29), .clk(CLK), .Q(register_30_q));  // open: clr
  Register #(.width(32)) register_31 (.D(in_3), .en(demultiplexer_1_out30), .clk(CLK), .Q(register_31_q));  // open: clr
  Register #(.width(32)) register_32 (.D(in_3), .en(demultiplexer_1_out31), .clk(CLK), .Q(register_32_q));  // open: clr
  Multiplexer #(.select(5), .width(32)) multiplexer_1 (
    .in0(register_1_q), .in1(register_2_q), .in2(register_3_q), .in3(register_4_q), .in4(register_5_q),
    .in5(register_6_q), .in6(register_7_q), .in7(register_8_q), .in8(register_9_q), .in9(register_10_q),
    .in10(register_11_q), .in11(register_12_q), .in12(register_13_q), .in13(register_14_q),
    .in14(register_15_q), .in15(register_16_q), .in16(register_17_q), .in17(register_18_q),
    .in18(register_19_q), .in19(register_20_q), .in20(register_21_q), .in21(register_22_q),
    .in22(register_23_q), .in23(register_24_q), .in24(register_25_q), .in25(register_26_q),
    .in26(register_27_q), .in27(register_28_q), .in28(register_29_q), .in29(register_30_q),
    .in30(register_31_q), .in31(register_32_q), .out(out_7), .sel(in_1));
  Multiplexer #(.select(5), .width(32)) multiplexer_2 (
    .in0(register_1_q), .in1(register_2_q), .in2(register_3_q), .in3(register_4_q), .in4(register_5_q),
    .in5(register_6_q), .in6(register_7_q), .in7(register_8_q), .in8(register_9_q), .in9(register_10_q),
    .in10(register_11_q), .in11(register_12_q), .in12(register_13_q), .in13(register_14_q),
    .in14(register_15_q), .in15(register_16_q), .in16(register_17_q), .in17(register_18_q),
    .in18(register_19_q), .in19(register_20_q), .in20(register_21_q), .in21(register_22_q),
    .in22(register_23_q), .in23(register_24_q), .in24(register_25_q), .in25(register_26_q),
    .in26(register_27_q), .in27(register_28_q), .in28(register_29_q), .in29(register_30_q),
    .in30(register_31_q), .in31(register_32_q), .out(out_8), .sel(in_4));

  // Notes on the sheet:
  //   RegWrite
  //   RD
  //   Data
  //   RS
  //   RT
  //   A
  //   B
endmodule

module ALU (
  input  [31:0] in_1,
  input  [31:0] in_2,
  input  [4:0] in_3,
  input  [3:0] in_4,
  output ZERO,
  output [31:0] out_6
);

  wire comparator_1_lt;
  wire [31:0] adder_1_out, and_1_out, bit_extender_1_out, not_1_out, or_1_out, shifter_1_out, shifter_2_out,
       shifter_3_out, subtractor_1_out, xor_1_out;

  Adder #(.width(32)) adder_1 (.a(in_1), .b(in_2), .out(adder_1_out));  // open: cin, cout
  Subtractor #(.width(32)) subtractor_1 (.a(in_1), .b(in_2), .out(subtractor_1_out));  // open: bin, bout
  Shifter #(.width(32)) shifter_1 (.in(in_1), .\dist (in_3), .out(shifter_1_out));
  Shifter #(.shift("lr"), .width(32)) shifter_2 (.in(in_1), .\dist (in_3), .out(shifter_2_out));
  Shifter #(.shift("ar"), .width(32)) shifter_3 (.in(in_1), .\dist (in_3), .out(shifter_3_out));
  assign and_1_out = in_1 & in_2;  // AND_Gate and_1, 32 bits wide
  assign or_1_out = in_1 | in_2;  // OR_Gate or_1, 32 bits wide
  assign xor_1_out = in_1 ^ in_2;  // XOR_Gate xor_1, 32 bits wide
  assign not_1_out = ~in_1;  // NOT_Gate not_1, 32 bits wide
  Comparator #(.width(32)) comparator_1 (.a(in_1), .b(in_2), .lt(comparator_1_lt));  // open: gt, eq
  assign bit_extender_1_out = {{31{comparator_1_lt}}, comparator_1_lt};  // Bit_Extender bit_extender_1
  Multiplexer #(.select(4), .width(32)) multiplexer_1 (
    .in0(adder_1_out), .in1(subtractor_1_out), .in2(shifter_1_out), .in3(shifter_2_out), .in4(shifter_3_out),
    .in5(and_1_out), .in6(or_1_out), .in7(xor_1_out), .in8(not_1_out), .in9(bit_extender_1_out), .out(out_6),
    .sel(in_4));  // open: in10, in11, in12, in13, in14, in15
  nor nor_1 (ZERO, out_6[0], out_6[1], out_6[2], out_6[3], out_6[4], out_6[5], out_6[6], out_6[7], out_6[8], out_6[9], out_6[10], out_6[11], out_6[12], out_6[13], out_6[14], out_6[15], out_6[16], out_6[17], out_6[18], out_6[19], out_6[20], out_6[21], out_6[22], out_6[23], out_6[24], out_6[25], out_6[26], out_6[27], out_6[28], out_6[29], out_6[30], out_6[31]);

  // Notes on the sheet:
  //   A
  //   B
  //   SHAMT
  //   ALUOP
  //   S
endmodule

module IM (
  input  [15:0] in_1,
  output [31:0] out_2
);

  // ROM #(.addrWidth(16), .line("quad")) rom_1: pin names not known; wires that end beside it: in_1, out_2[31:24], out_2[23:16], out_2[15:8], out_2[7:0]

  // Notes on the sheet:
  //   contents of rom_1 (hex, n*v repeats v):
  //   0 1 0 6 0 21 10 0 0 42 18 0 0 63 20
endmodule

module IF_ID (
  input  in_1,
  input  [31:0] in_2,
  input  [15:0] in_3,
  input  in_4,
  output [31:0] out_5,
  output [15:0] out_6
);

  Register #(.width(32)) register_1 (.D(in_2), .en(in_1), .clk(in_4), .Q(out_5));  // open: clr
  Register #(.width(16)) register_2 (.D(in_3), .en(in_1), .clk(in_4), .Q(out_6));  // open: clr

  // Notes on the sheet:
  //   INSTRUCTION
  //   NEW PC
  //   IF_ID WRITE
  //   CLK
endmodule

module IntructionFormater (
  input  [31:0] in_1,
  output [5:0] out_2,
  output [4:0] out_3,
  output [4:0] out_4,
  output [15:0] out_5,
  output [4:0] out_6,
  output [4:0] out_7,
  output [5:0] out_8
);


  assign out_2 = in_1[5:0];
  assign out_3 = in_1[10:6];
  assign out_4 = in_1[15:11];
  assign out_5 = in_1[15:0];
  assign out_6 = in_1[20:16];
  assign out_7 = in_1[25:21];
  assign out_8 = in_1[31:26];

  // Notes on the sheet:
  //   Instuction
  //   Func
  //   Shamt
  //   RD
  //   Immediate
  //   RT
  //   RS
  //   Opcode
endmodule

module ControlUnit (
  input  [5:0] in_1,
  input  [5:0] in_2,
  output out_3,
  output out_4,
  output out_5,
  output out_6,
  output out_7,
  output out_8,
  output out_9,
  output [3:0] out_10
);


  // Notes on the sheet:
  //   OPCODE
  //   FUNCT
  //   ALUOP
endmodule

module ID_EX (
  input  in_1,
  input  in_2,
  input  in_3,
  input  in_4,
  input  RegDst,
  input  Branch,
  input  ALUsrc,
  input  [3:0] in_8,
  input  [4:0] in_9,
  input  [31:0] in_10,
  input  [31:0] in_11,
  input  [15:0] in_12,
  input  [15:0] in_13,
  input  [4:0] in_14,
  input  [4:0] in_15,
  input  [4:0] in_16,
  input  CLK,
  output out_18,
  output out_19,
  output out_20,
  output out_21,
  output out_22,
  output out_23,
  output out_24,
  output [3:0] out_25,
  output [4:0] out_26,
  output [31:0] out_27,
  output [31:0] out_28,
  output [15:0] out_29,
  output [15:0] out_30,
  output [4:0] out_31,
  output [4:0] out_32,
  output [4:0] out_33
);

  Register #(.width(16)) register_1 (
    .D({in_9, in_8, ALUsrc, Branch, RegDst, in_4, in_3, in_2, in_1}), .en(1'b1), .clk(CLK),
    .Q({out_26, out_25, out_24, out_23, out_22, out_21, out_20, out_19, out_18}));  // open: clr
  Register #(.width(32)) register_2 (.D(in_10), .en(1'b1), .clk(CLK), .Q(out_27));  // open: clr
  Register #(.width(32)) register_3 (.D(in_11), .en(1'b1), .clk(CLK), .Q(out_28));  // open: clr
  Register #(.width(16)) register_4 (.D(in_12), .en(1'b1), .clk(CLK), .Q(out_29));  // open: clr
  Register #(.width(16)) register_5 (.D(in_13), .en(1'b1), .clk(CLK), .Q(out_30));  // open: clr
  Register #(.width(5)) register_6 (.D(in_14), .en(1'b1), .clk(CLK), .Q(out_31));  // open: clr
  Register #(.width(5)) register_7 (.D(in_15), .en(1'b1), .clk(CLK), .Q(out_32));  // open: clr
  Register #(.width(5)) register_8 (.D(in_16), .en(1'b1), .clk(CLK), .Q(out_33));  // open: clr

  // Notes on the sheet:
  //   MemRead
  //   MemWrite
  //   MemToReg
  //   RegWrite
  //   ALUop
  //   Shamt
  //   A
  //   B
  //   Immediate
  //   NewPC
  //   RS
  //   RT
  //   RD
endmodule

module EX_MEM (
  input  in_1,
  input  in_2,
  input  in_3,
  input  in_4,
  input  Branch,
  input  Zero,
  input  [31:0] in_7,
  input  [15:0] in_8,
  input  [31:0] in_9,
  input  [4:0] in_10,
  input  CLK,
  output out_12,
  output out_13,
  output out_14,
  output out_15,
  output out_16,
  output out_17,
  output [31:0] out_18,
  output [15:0] out_19,
  output [31:0] out_20,
  output [4:0] out_21
);

  Register #(.width(1)) register_1 (.D(in_1), .en(1'b1), .clk(CLK), .Q(out_12));  // open: clr
  Register #(.width(1)) register_2 (.D(in_2), .en(1'b1), .clk(CLK), .Q(out_13));  // open: clr
  Register #(.width(1)) register_3 (.D(in_3), .en(1'b1), .clk(CLK), .Q(out_14));  // open: clr
  Register #(.width(1)) register_4 (.D(in_4), .en(1'b1), .clk(CLK), .Q(out_15));  // open: clr
  Register #(.width(1)) register_5 (.D(Branch), .en(1'b1), .clk(CLK), .Q(out_16));  // open: clr
  Register #(.width(1)) register_6 (.D(Zero), .en(1'b1), .clk(CLK), .Q(out_17));  // open: clr
  Register #(.width(32)) register_7 (.D(in_7), .en(1'b1), .clk(CLK), .Q(out_18));  // open: clr
  Register #(.width(16)) register_8 (.D(in_8), .en(1'b1), .clk(CLK), .Q(out_19));  // open: clr
  Register #(.width(32)) register_9 (.D(in_9), .en(1'b1), .clk(CLK), .Q(out_20));  // open: clr
  Register #(.width(5)) register_10 (.D(in_10), .en(1'b1), .clk(CLK), .Q(out_21));  // open: clr

  // Notes on the sheet:
  //   MemWrite
  //   MemToReg
  //   ALUout
  //   BeqAddress
  //   WriteData
  //   RD
  //   MemRead
  //   RegWrite
endmodule

module DM (
  input  [31:0] in_1,
  input  in_2,
  input  in_3,
  input  CLK,
  input  [31:0] in_5,
  output [31:0] out_6
);

  RAM #(.addrWidth(16), .dataWidth(32)) ram_1 (
    .addr(in_1[15:0]), .we(in_2), .oe(in_3), .clk(CLK), .din(in_5), .dout(out_6));

  // Notes on the sheet:
  //   Address
  //   MemWrite
  //   MemRead
  //   Data
endmodule

module MEM_WB (
  input  in_1,
  input  in_2,
  input  [31:0] in_3,
  input  [31:0] in_4,
  input  [4:0] in_5,
  input  CLK,
  output out_7,
  output out_8,
  output [31:0] out_9,
  output [31:0] out_10,
  output [4:0] out_11
);

  Register #(.width(1)) register_1 (.D(in_1), .en(1'b1), .clk(CLK), .Q(out_7));  // open: clr
  Register #(.width(1)) register_2 (.D(in_2), .en(1'b1), .clk(CLK), .Q(out_8));  // open: clr
  Register #(.width(32)) register_3 (.D(in_3), .en(1'b1), .clk(CLK), .Q(out_9));  // open: clr
  Register #(.width(32)) register_4 (.D(in_4), .en(1'b1), .clk(CLK), .Q(out_10));  // open: clr
  Register #(.width(5)) register_5 (.D(in_5), .en(1'b1), .clk(CLK), .Q(out_11));  // open: clr

  // Notes on the sheet:
  //   MemToReg
  //   RegWrite
  //   ReadData
  //   ALUout
  //   RD
endmodule

module HazardUnit (
  input  [4:0] in_1,
  input  [31:0] MemRead,
  input  in_3,
  output out_4,
  output Flush,
  output out_6
);

  wire and_1_out, comparator_1_eq, nor_1_out;

  nor nor_1 (nor_1_out, in_1[0], in_1[1], in_1[2], in_1[3], in_1[4]);
  Comparator #(.width(5)) comparator_1 (.a(in_1), .b(MemRead[15:11]), .eq(comparator_1_eq));  // open: gt, lt
  and and_1 (and_1_out, comparator_1_eq, in_3);
  Multiplexer multiplexer_1 (.in0(and_1_out), .in1(1'b0), .out(Flush), .sel(nor_1_out));
  not not_1 (out_4, Flush);
  not not_2 (out_6, Flush);

  // Notes on the sheet:
  //   Instruction
  //   RD
  //   IF/IDwrite
  //   PCwrite
endmodule

module ForwardingUnit (
  input  in_1,
  input  [4:0] in_2,
  input  [4:0] in_3,
  input  [4:0] in_4,
  input  in_5,
  input  [4:0] in_6,
  output [1:0] out_7,
  output [1:0] out_8
);


  // Notes on the sheet:
  //   RS
  //   RT
  //   WBRD
  //   WB
endmodule
